// Digital circuit C2-SM.dig as structural Verilog
module C2_SM (
  input  A_2,
  input  A_1,
  input  A_0,
  output R_2,
  output R_1,
  output R_0,
  output E
);

  wire and_1_out, and_2_out, and_3_out, not_1_out, not_2_out, not_3_out;

  not not_1 (not_1_out, A_2);
  not not_2 (not_2_out, A_1);
  not not_3 (not_3_out, A_0);
  and and_1 (and_1_out, not_1_out, A_1);
  and and_2 (and_2_out, A_2, not_2_out);
  and and_3 (and_3_out, A_1, not_3_out);
  and and_4 (E, A_2, not_2_out, not_3_out);
  or or_1 (R_1, and_1_out, and_2_out, and_3_out);

  assign R_0 = A_0;
  assign R_2 = A_2;
endmodule
