// Digital circuit Decodificador2-4.dig as structural Verilog
module Decodificador2_4 (
  input  X_0,
  input  E,
  input  X_1,
  input  X_2,
  input  X_3,
  output Y_0,
  output Y_1,
  output Y_2,
  output Y_3,
  output Y_4,
  output Y_5,
  output Y_6,
  output Y_7,
  output Y_8,
  output Y_9,
  output Y_10,
  output Y_11,
  output Y_12,
  output Y_13,
  output Y_14,
  output Y_15
);

  wire not_1_out, not_2_out, not_3_out, not_4_out;

  not not_1 (not_1_out, X_0);
  not not_2 (not_2_out, X_1);
  not not_3 (not_3_out, X_2);
  not not_4 (not_4_out, X_3);
  and and_1 (Y_0, not_1_out, not_2_out, not_3_out, not_4_out, E);
  and and_2 (Y_1, X_0, not_2_out, not_3_out, not_4_out, E);
  and and_3 (Y_2, not_1_out, X_1, not_3_out, not_4_out, E);
  and and_4 (Y_3, X_1, X_0, not_3_out, not_4_out, E);
  and and_5 (Y_4, not_1_out, not_2_out, X_2, not_4_out, E);
  and and_6 (Y_5, X_0, not_2_out, X_2, not_4_out, E);
  and and_7 (Y_6, not_1_out, X_1, X_2, not_4_out, E);
  and and_8 (Y_7, X_0, X_1, X_2, not_4_out, E);
  and and_9 (Y_8, not_1_out, not_2_out, not_3_out, X_3, E);
  and and_10 (Y_9, X_0, not_2_out, not_3_out, X_3, E);
  and and_11 (Y_10, not_1_out, X_1, not_3_out, X_3, E);
  and and_12 (Y_11, X_1, X_0, not_3_out, X_3, E);
  and and_13 (Y_12, not_1_out, not_2_out, X_2, X_3, E);
  and and_14 (Y_13, X_0, not_2_out, X_2, X_3, E);
  and and_15 (Y_14, not_1_out, X_1, X_2, X_3, E);
  and and_16 (Y_15, X_0, X_1, X_2, X_3, E);
endmodule
