// Digital circuit Entrega3-Resta.dig as structural Verilog
module Entrega3_Resta (
  input  A_0,
  input  B_0,
  input  A_1,
  input  B_1,
  input  A_2,
  input  B_2,
  output R_0,
  output R_1,
  output R_2,
  output E
);

  wire add_1_c_o, add_2_c_o, and_1_out, and_2_out, not_1_out, not_2_out, not_3_out, not_4_out, not_5_out,
       not_6_out;

  Add add_1 (.a(A_0), .b(not_1_out), .c_i(1'b1), .s(R_0), .c_o(add_1_c_o));
  not not_1 (not_1_out, B_0);
  Add add_2 (.a(A_1), .b(not_2_out), .c_i(add_1_c_o), .s(R_1), .c_o(add_2_c_o));
  not not_2 (not_2_out, B_1);
  not not_3 (not_3_out, B_2);
  Add add_3 (.a(A_2), .b(not_3_out), .c_i(add_2_c_o), .s(R_2));  // open: c_o
  not not_4 (not_4_out, A_2);
  not not_5 (not_5_out, B_2);
  not not_6 (not_6_out, R_2);
  and and_1 (and_1_out, not_4_out, B_2, R_2);
  and and_2 (and_2_out, A_2, not_5_out, not_6_out);
  or or_1 (E, and_1_out, and_2_out);
endmodule
