// Digital circuit Casi_Mux8-3.dig as structural Verilog
module Casi_Mux8_3 (
  input  in_2,
  input  in_3,
  input  in_4,
  input  in_5,
  input  in_6,
  input  in_7,
  input  in_8,
  input  in_9,
  input  in_10,
  input  in_11,
  input  in_12,
  output out_1
);

  wire and_1_out, and_2_out, and_3_out, and_4_out, and_5_out, and_6_out, and_7_out, and_8_out;

  and and_1 (and_1_out, in_5, in_4, in_2, in_3);
  and and_2 (and_2_out, in_6, in_4, in_2, in_3);
  and and_3 (and_3_out, in_7, in_4, in_2, in_3);
  and and_4 (and_4_out, in_8, in_4, in_2, in_3);
  and and_5 (and_5_out, in_9, in_4, in_4, in_4);
  and and_6 (and_6_out, in_10, in_4, in_4, in_2);
  and and_7 (and_7_out, in_11, in_4, in_2, in_3);
  and and_8 (and_8_out, in_12, in_4, in_2, in_3);
  or or_1 (out_1, and_1_out, and_2_out, and_3_out, and_4_out, and_5_out, and_6_out, and_7_out, and_8_out);
endmodule
