// Digital circuit Entrega4-Comparador.dig as structural Verilog
module Entrega4_Comparador (
  input  A_0,
  input  A_1,
  input  A_2,
  input  B_0,
  input  B_1,
  input  B_2,
  output R_2,
  output R_1,
  output R_0,
  output E
);

  Comparator #(.Signed("true"), .Bits(3)) comparator_1 (
    .a({A_2, A_1, A_0}), .b({B_2, B_1, B_0}), .gt(R_0), .eq(R_1), .lt(R_2));

  assign E = 1'b0;
endmodule
