// Digital circuit Entrega6-Primos.dig as structural Verilog
module Entrega6_Primos (
  input  A_0,
  input  A_1,
  input  A_2,
  output R_0,
  output R_1,
  output R_2,
  output E
);

  wire and_1_out, and_2_out, not_1_out;

  not not_1 (not_1_out, A_2);
  and and_1 (and_1_out, not_1_out, A_1);
  and and_2 (and_2_out, A_2, A_0);
  or or_1 (R_0, and_1_out, and_2_out);

  assign E = 1'b0;
  assign R_1 = R_0;
  assign R_2 = R_0;
endmodule
