// Digital circuit Practica10.3.dig as structural Verilog
module Practica10_3 (
  input  [3:0] X_2,
  input  [3:0] X_3,
  input  [2:0] X_0,
  output [2:0] out_4
);

  wire [2:0] not_1_out;
  wire [2:1] undriven;

  not not_1 (not_1_out[0], X_0[0]);
  Multiplexer #(.Bits(3), .Selector_Bits(2)) multiplexer_1 (
    .sel(X_2[1:0]), .in_0(X_0), .in_1({undriven, 1'b0}), .in_2(not_1_out), .in_3(X_0), .out(out_4));
  // Pins of 1 and 4 bits meet at X_2
  // Pins of 1 and 4 bits meet at X_3
  // Pins of 1 and 3 bits meet at X_0
  // Pins of 1 and 3 bits meet at not_1_out
  // Pins of 1 and 3 bits meet at {undriven, 1'b0}
  // Pins of 1 and 3 bits meet at out_4
  // Pins of 2 and 8 bits meet at {X_3, X_2}
endmodule
