// Digital circuit Practica10.dig as structural Verilog
module Practica10 (
  input  X_1,
  input  X_2,
  input  X_3,
  input  X_0,
  output out_5
);

  wire not_1_out, not_2_out, not_3_out;

  Mux8_1 mux8_1_1 (
    .Y(out_5), .S_2(X_3), .S_1(X_2), .S_0(X_1), .D_0(not_1_out), .D_1(X_0), .D_2(1'b0), .D_3(not_2_out),
    .D_4(X_0), .D_5(1'b0), .D_6(not_3_out), .D_7(X_0));
  not not_1 (not_1_out, X_0);
  not not_2 (not_2_out, X_0);
  not not_3 (not_3_out, X_0);
endmodule
