// Digital circuit Practica4b.dig as structural Verilog
module Practica4b (
  input  B,
  input  C,
  input  D,
  input  A,
  output out_5
);

  wire decodificador2_4_1_p6, decodificador2_4_1_p7, decodificador2_4_1_p8, decodificador2_4_1_p9,
       decodificador2_4_1_p10;

  // Decodificador2_4 decodificador2_4_1: pin names not known; wires that end beside it: D, C, B, A, 1'b1, decodificador2_4_1_p6, decodificador2_4_1_p7, decodificador2_4_1_p8, decodificador2_4_1_p9, decodificador2_4_1_p10
  or or_1 (out_5, decodificador2_4_1_p6, decodificador2_4_1_p7, decodificador2_4_1_p8, decodificador2_4_1_p9, decodificador2_4_1_p10);
endmodule
