// Digital circuit Practica4c.dig as structural Verilog
module Practica4c (
  input  A,
  input  B,
  input  C,
  input  D,
  output out_1
);

  wire not_1_out;

  not not_1 (not_1_out, D);
  Mux8_1 mux8_1_1 (
    .Y(out_1), .S_2(A), .S_1(B), .S_0(C), .D_0(1'b0), .D_1(not_1_out), .D_2(D), .D_3(D), .D_4(1'b0),
    .D_5(1'b0), .D_6(D), .D_7(not_1_out));
endmodule
