// Digital circuit solucio.dig as structural Verilog
module solucio (
  input  A_2,
  input  A_1,
  input  A_0,
  input  B_2,
  input  B_1,
  input  B_0,
  input  C_2,
  input  C_1,
  input  C_0,
  output R_0,
  output R_1,
  output R_2,
  output E
);

  wire [3:0] c2_sm_1_r_1, entrega3_resta_1_r_0, entrega4_comparador_1_r_1, entrega5_pordos_1_r_0,
       entrega6_primos_1_r_0, sm_c2_1_r_1;

  SM_C2 sm_c2_1 (
    .A_2(A_2), .A_1(A_1), .A_0(A_0), .R_2(sm_c2_1_r_1[2]), .R_1(sm_c2_1_r_1[1]), .R_0(sm_c2_1_r_1[0]),
    .E(sm_c2_1_r_1[3]));
  C2_SM c2_sm_1 (
    .A_2(A_2), .A_1(A_1), .A_0(A_0), .R_2(c2_sm_1_r_1[2]), .R_1(c2_sm_1_r_1[1]), .R_0(c2_sm_1_r_1[0]),
    .E(c2_sm_1_r_1[3]));
  Entrega3_Resta entrega3_resta_1 (
    .A_0(A_0), .B_0(A_1), .A_1(A_2), .B_1(B_0), .A_2(B_1), .B_2(B_2), .R_0(entrega3_resta_1_r_0[0]),
    .R_1(entrega3_resta_1_r_0[1]), .R_2(entrega3_resta_1_r_0[2]), .E(entrega3_resta_1_r_0[3]));
  Entrega4_Comparador entrega4_comparador_1 (
    .A_0(A_0), .A_1(A_1), .A_2(A_2), .B_0(B_0), .B_1(B_1), .B_2(B_2), .R_2(entrega4_comparador_1_r_1[2]),
    .R_1(entrega4_comparador_1_r_1[1]), .R_0(entrega4_comparador_1_r_1[0]), .E(entrega4_comparador_1_r_1[3]));
  Entrega5_PorDos entrega5_pordos_1 (
    .A_0(A_0), .A_1(A_1), .A_2(A_2), .R_0(entrega5_pordos_1_r_0[0]), .R_1(entrega5_pordos_1_r_0[1]),
    .R_2(entrega5_pordos_1_r_0[2]), .E(entrega5_pordos_1_r_0[3]));
  Entrega6_Primos entrega6_primos_1 (
    .A_0(A_0), .A_1(A_1), .A_2(A_2), .R_0(entrega6_primos_1_r_0[0]), .R_1(entrega6_primos_1_r_0[1]),
    .R_2(entrega6_primos_1_r_0[2]), .E(entrega6_primos_1_r_0[3]));
  Multiplexer #(.Selector_Bits(3), .Bits(4)) multiplexer_1 (
    .sel({C_2, C_1, C_0}), .in_0(sm_c2_1_r_1), .in_1(c2_sm_1_r_1), .in_2(entrega3_resta_1_r_0),
    .in_3(entrega4_comparador_1_r_1), .in_4(entrega5_pordos_1_r_0), .in_5(entrega6_primos_1_r_0),
    .in_6(4'b0000), .in_7(4'b0000), .out({E, R_2, R_1, R_0}));
endmodule
