// Digital circuit Principal.dig as structural Verilog
module Principal (
  input  X_1,
  input  X_0,
  input  clk,
  output VERD,
  output VERMELL,
  output GROC,
  output BLAU
);

  wire and_1_out, and_2_out, and_3_out, and_4_out, and_5_out, and_6_out, and_7_out, and_8_out, and_9_out,
       and_10_out, and_11_out, and_12_out, and_13_out, and_14_out, and_15_out, FF_0_nq, FF_0_q, FF_1_nq,
       FF_1_q, FF_2_nq, not_1_out, not_2_out, or_1_out, or_2_out, or_3_out;

  not not_1 (not_1_out, X_1);
  not not_2 (not_2_out, X_0);
  and and_1 (and_1_out, FF_2_nq, X_1);
  and and_2 (and_2_out, FF_1_q, FF_0_nq, X_0);
  and and_3 (and_3_out, FF_1_nq, FF_0_nq, X_1);
  and and_4 (and_4_out, FF_1_q, FF_0_q, not_1_out, not_2_out);
  and and_5 (and_5_out, FF_2_nq, FF_0_q, X_0);
  and and_6 (and_6_out, FF_2_nq, FF_1_nq, FF_0_q, not_1_out);
  and and_7 (and_7_out, FF_1_q, FF_0_nq, not_1_out, not_2_out);
  and and_8 (and_8_out, FF_1_nq, X_0);
  and and_9 (and_9_out, not_2_out, FF_0_nq);
  and and_10 (and_10_out, FF_2_nq, X_1);
  and and_11 (and_11_out, BLAU, not_1_out);
  or or_1 (or_1_out, and_1_out, and_2_out, and_3_out, and_4_out);
  or or_2 (or_2_out, and_5_out, and_6_out, and_7_out);
  or or_3 (or_3_out, and_8_out, and_9_out, and_10_out, and_11_out);
  D_FF FF_2 (.D(or_1_out), .C(clk), .Q(BLAU), .nQ(FF_2_nq));
  D_FF FF_1 (.D(or_2_out), .C(clk), .Q(FF_1_q), .nQ(FF_1_nq));
  D_FF FF_0 (.D(or_3_out), .C(clk), .Q(FF_0_q), .nQ(FF_0_nq));
  and and_12 (and_12_out, BLAU, FF_0_q);
  and and_13 (and_13_out, FF_1_q, FF_0_nq);
  and and_14 (and_14_out, BLAU, FF_0_q);
  and and_15 (and_15_out, FF_1_q, FF_0_q);
  and and_16 (VERD, FF_1_nq, FF_0_q);
  or or_4 (VERMELL, and_12_out, and_13_out);
  or or_5 (GROC, and_14_out, and_15_out);
  LED LED_VERD (.in(VERD));
  LED LED_VERMELL (.in(VERMELL));
  LED LED_GROC (.in(GROC));
  LED LED_BLAU (.in(BLAU));
endmodule
