// Digital circuit SM-C2.dig as structural Verilog
module SM_C2 (
  input  A_2,
  input  A_1,
  input  A_0,
  output R_2,
  output R_1,
  output R_0,
  output E
);

  wire and_1_out, and_2_out, and_3_out, and_4_out, and_5_out, not_1_out, not_2_out, not_3_out;

  not not_1 (not_1_out, A_2);
  not not_2 (not_2_out, A_1);
  not not_3 (not_3_out, A_0);
  and and_1 (and_1_out, A_2, not_2_out, A_0);
  and and_2 (and_2_out, A_2, A_1);
  and and_3 (and_3_out, A_0, A_2);
  and and_4 (and_4_out, not_1_out, A_1);
  and and_5 (and_5_out, A_1, not_3_out);
  or or_1 (R_2, and_2_out, and_3_out);
  or or_2 (R_1, and_4_out, and_5_out, and_1_out);

  assign E = 1'b0;
  assign R_0 = A_0;
endmodule
