// Digital circuit 000.dig as structural Verilog
module _000 (
  input  A2,
  input  A1,
  input  A0,
  output R0,
  output R1,
  output R2,
  output E
);

  wire and_1_out, and_2_out, and_3_out, not_1_out, not_2_out, not_3_out, or_1_out;

  not not_1 (not_1_out, A2);
  not not_2 (not_2_out, A1);
  not not_3 (not_3_out, A0);
  or or_1 (or_1_out, A1, A0);
  and and_1 (and_1_out, A2, not_2_out, A0);
  and and_2 (and_2_out, not_1_out, A1);
  and and_3 (and_3_out, A1, not_3_out);
  and and_4 (R2, A2, or_1_out);
  or or_2 (R1, and_1_out, and_2_out, and_3_out);

  assign E = 1'b0;
  assign R0 = A0;
endmodule

/* Test case SM - C2:
A2 A1 A0 E R2 R1 R0
1  1  1  0  1  0  1
1  1  0  0  1  1  0
1  0  1  0  1  1  1
1  0  0  0  0  0  0
0  0  0  0  0  0  0
0  0  1  0  0  0  1
0  1  0  0  0  1  0
0  1  1  0  0  1  1
*/
