// Digital circuit 010.dig as structural Verilog
module _010 (
  input  A0,
  input  B0,
  input  A1,
  input  B1,
  input  A2,
  input  B2,
  output R0,
  output R1,
  output R2,
  output E
);

  wire add_1_c_o, add_2_c_o, and_1_out, and_2_out, not_1_out, not_2_out, not_3_out, not_4_out, not_5_out,
       not_6_out;

  not not_1 (not_1_out, B0);
  not not_2 (not_2_out, B1);
  not not_3 (not_3_out, B2);
  and and_1 (and_1_out, R2, not_4_out, not_5_out);
  not not_4 (not_4_out, A2);
  not not_5 (not_5_out, not_3_out);
  and and_2 (and_2_out, not_6_out, A2, not_3_out);
  not not_6 (not_6_out, R2);
  Add add_1 (.a(A0), .b(not_1_out), .c_i(1'b1), .s(R0), .c_o(add_1_c_o));
  Add add_2 (.a(A1), .b(not_2_out), .c_i(add_1_c_o), .s(R1), .c_o(add_2_c_o));
  Add add_3 (.a(A2), .b(not_3_out), .c_i(add_2_c_o), .s(R2));  // open: c_o
  or or_1 (E, and_1_out, and_2_out);
endmodule
