// Digital circuit 011.dig as structural Verilog
module _011 (
  input  A0,
  input  A1,
  input  A2,
  input  B0,
  input  B1,
  input  B2,
  output R0,
  output R1,
  output R2,
  output E
);

  Comparator #(.Signed("true"), .Bits(3)) comparator_1 (.a({A2, A1, A0}), .b({B2, B1, B0}), .gt(R0), .eq(R1), .lt(R2));

  assign E = 1'b0;
endmodule
