// Digital circuit 101.dig as structural Verilog
module _101 (
  input  A2,
  input  A1,
  input  A0,
  output R0,
  output R1,
  output R2,
  output E
);

  wire and_1_out, and_2_out, not_1_out;

  not not_1 (not_1_out, A2);
  and and_1 (and_1_out, A2, A0);
  and and_2 (and_2_out, not_1_out, A1);
  or or_1 (R0, and_1_out, and_2_out);

  assign E = 1'b0;
  assign R1 = R0;
  assign R2 = R0;
endmodule

/* Test case NUMEROS PRIMOS:
A2 A1 A0 E R2 R1 R0
0  0  0  0  0  0  0
0  0  1  0  0  0  0
0  1  0  0  1  1  1
0  1  1  0  1  1  1
1  0  0  0  0  0  0
1  0  1  0  1  1  1
1  1  0  0  0  0  0
1  1  1  0  1  1  1
*/
