// Digital circuit solucio.dig as structural Verilog
module solucio (
  input  C2,
  input  C1,
  input  C0,
  input  A2,
  input  A1,
  input  A0,
  input  B2,
  input  B1,
  input  B0,
  output E,
  output R2,
  output R1,
  output R0
);

  wire [3:0] _000_1_r1, _001_1_r0, _010_1_r0, _011_1_r0, _100_1_r0, _101_1_r0;

  _000 _000_1 (.A2(A2), .A1(A1), .A0(A0), .R0(_000_1_r1[0]), .R1(_000_1_r1[1]), .R2(_000_1_r1[2]), .E(_000_1_r1[3]));
  _001 _001_1 (.A2(A2), .A1(A1), .A0(A0), .R0(_001_1_r0[0]), .R1(_001_1_r0[1]), .R2(_001_1_r0[2]), .E(_001_1_r0[3]));
  _010 _010_1 (
    .A0(A0), .B0(B0), .A1(A1), .B1(B1), .A2(A2), .B2(B2), .R0(_010_1_r0[0]), .R1(_010_1_r0[1]),
    .R2(_010_1_r0[2]), .E(_010_1_r0[3]));
  _011 _011_1 (
    .A0(A0), .A1(A1), .A2(A2), .B0(B0), .B1(B1), .B2(B2), .R0(_011_1_r0[0]), .R1(_011_1_r0[1]),
    .R2(_011_1_r0[2]), .E(_011_1_r0[3]));
  _100 _100_1 (.A0(A0), .A1(A1), .A2(A2), .R0(_100_1_r0[0]), .R1(_100_1_r0[1]), .R2(_100_1_r0[2]), .E(_100_1_r0[3]));
  _101 _101_1 (.A2(A2), .A1(A1), .A0(A0), .R0(_101_1_r0[0]), .R1(_101_1_r0[1]), .R2(_101_1_r0[2]), .E(_101_1_r0[3]));
  Multiplexer #(.Selector_Bits(3), .Bits(4)) multiplexer_1 (
    .sel({C2, C1, C0}), .in_0(_000_1_r1), .in_1(_001_1_r0), .in_2(_010_1_r0), .in_3(_011_1_r0),
    .in_4(_100_1_r0), .in_5(_101_1_r0), .in_6(4'b0000), .in_7(4'b0000), .out({E, R2, R1, R0}));
endmodule

/* Test case SM - C2:
C2 C1 C0 A2 A1 A0 B2 B1 B0 E R2 R1 R0
0  0  0  1  1  1  X  X  X  0  1  0  1
0  0  0  1  1  0  X  X  X  0  1  1  0
0  0  0  1  0  1  X  X  X  0  1  1  1
0  0  0  1  0  0  X  X  X  0  0  0  0
0  0  0  0  0  0  X  X  X  0  0  0  0
0  0  0  0  0  1  X  X  X  0  0  0  1
0  0  0  0  1  0  X  X  X  0  0  1  0
0  0  0  0  1  1  X  X  X  0  0  1  1
*/

/* Test case A-B:
C2 C1 C0 A2 A1 A0 B2 B1 B0 E R2 R1 R0
0  1  0  1  0  0  1  0  0  0  0  0  0
0  1  0  1  0  0  1  0  1  0  1  1  1
0  1  0  1  0  0  1  1  0  0  1  1  0
0  1  0  1  0  0  1  1  1  0  1  0  1
0  1  0  1  0  0  0  0  0  0  1  0  0
0  1  0  1  0  0  0  0  1  1  X  X  X
0  1  0  1  0  0  0  1  0  1  X  X  X
0  1  0  1  0  0  0  1  1  1  X  X  X
0  1  0  1  0  1  1  0  0  0  0  0  1
0  1  0  1  0  1  1  0  1  0  0  0  0
0  1  0  1  0  1  1  1  0  0  1  1  1
0  1  0  1  0  1  1  1  1  0  1  1  0
0  1  0  1  0  1  0  0  0  0  1  0  1
0  1  0  1  0  1  0  0  1  0  1  0  0
0  1  0  1  0  1  0  1  0  1  X  X  X
0  1  0  1  0  1  0  1  1  1  X  X  X
0  1  0  1  1  0  1  0  0  0  0  1  0
0  1  0  1  1  0  1  0  1  0  0  0  1
0  1  0  1  1  0  1  1  0  0  0  0  0
0  1  0  1  1  0  1  1  1  0  1  1  1
0  1  0  1  1  0  0  0  0  0  1  1  0
0  1  0  1  1  0  0  0  1  0  1  0  1
0  1  0  1  1  0  0  1  0  0  1  0  0
0  1  0  1  1  0  0  1  1  1  X  X  X
0  1  0  1  1  1  1  0  0  0  0  1  1
0  1  0  1  1  1  1  0  1  0  0  1  0
0  1  0  1  1  1  1  1  0  0  0  0  1
0  1  0  1  1  1  1  1  1  0  0  0  0
0  1  0  1  1  1  0  0  0  0  1  1  1
0  1  0  1  1  1  0  0  1  0  1  1  0
0  1  0  1  1  1  0  1  0  0  1  0  1
0  1  0  1  1  1  0  1  1  0  1  0  0
0  1  0  0  0  0  1  0  0  1  X  X  X
0  1  0  0  0  0  1  0  1  0  0  1  1
0  1  0  0  0  0  1  1  0  0  0  1  0
0  1  0  0  0  0  1  1  1  0  0  0  1
0  1  0  0  0  0  0  0  0  0  0  0  0
0  1  0  0  0  0  0  0  1  0  1  1  1
0  1  0  0  0  0  0  1  0  0  1  1  0
0  1  0  0  0  0  0  1  1  0  1  0  1
0  1  0  0  0  1  1  0  0  1  X  X  X
0  1  0  0  0  1  1  0  1  1  X  X  X
0  1  0  0  0  1  1  1  0  0  0  1  1
0  1  0  0  0  1  1  1  1  0  0  1  0
0  1  0  0  0  1  0  0  0  0  0  0  1
0  1  0  0  0  1  0  0  1  0  0  0  0
0  1  0  0  0  1  0  1  0  0  1  1  1
0  1  0  0  0  1  0  1  1  0  1  1  0
0  1  0  0  1  0  1  0  0  1  X  X  X
0  1  0  0  1  0  1  0  1  1  X  X  X
0  1  0  0  1  0  1  1  0  1  X  X  X
0  1  0  0  1  0  1  1  1  0  0  1  1
0  1  0  0  1  0  0  0  0  0  0  1  0
0  1  0  0  1  0  0  0  1  0  0  0  1
0  1  0  0  1  0  0  1  0  0  0  0  0
0  1  0  0  1  0  0  1  1  0  1  1  1
0  1  0  0  1  1  1  0  0  1  X  X  X
0  1  0  0  1  1  1  0  1  1  X  X  X
0  1  0  0  1  1  1  1  0  1  X  X  X
0  1  0  0  1  1  1  1  1  1  X  X  X
0  1  0  0  1  1  0  0  0  0  0  1  1
0  1  0  0  1  1  0  0  1  0  0  1  0
0  1  0  0  1  1  0  1  0  0  0  0  1
0  1  0  0  1  1  0  1  1  0  0  0  0
*/

/* Test case A*2:
C2 C1 C0 A2 A1 A0 B2 B1 B0 E R2 R1 R0
1  0  0  1  0  0  X  X  X  1  0  0  0
1  0  0  1  0  1  X  X  X  1  0  1  0
1  0  0  1  1  0  X  X  X  1  1  0  0
1  0  0  1  1  1  X  X  X  1  1  1  0
1  0  0  0  0  0  X  X  X  0  0  0  0
1  0  0  0  0  1  X  X  X  0  0  1  0
1  0  0  0  1  0  X  X  X  0  1  0  0
1  0  0  0  1  1  X  X  X  0  1  1  0
*/

/* Test case C2- SM:
C2 C1 C0 A2 A1 A0 B2 B1 B0 E R2 R1 R0
0  0  1  1  0  0  X  X  X  1  X  X  X
0  0  1  1  0  1  X  X  X  0  1  1  1
0  0  1  1  1  0  X  X  X  0  1  1  0
0  0  1  1  1  1  X  X  X  0  1  0  1
0  0  1  0  0  0  X  X  X  0  0  0  0
0  0  1  0  0  1  X  X  X  0  0  0  1
0  0  1  0  1  0  X  X  X  0  0  1  0
0  0  1  0  1  1  X  X  X  0  0  1  1
*/

/* Test case Comparador:
C2 C1 C0 A2 A1 A0 B2 B1 B0 E R2 R1 R0
0  1  1  1  0  0  1  0  0  0  0  1  0
0  1  1  1  0  0  1  0  1  0  1  0  0
0  1  1  1  0  0  1  1  0  0  1  0  0
0  1  1  1  0  0  1  1  1  0  1  0  0
0  1  1  1  0  0  0  0  0  0  1  0  0
0  1  1  1  0  0  0  0  1  0  1  0  0
0  1  1  1  0  0  0  1  0  0  1  0  0
0  1  1  1  0  0  0  1  1  0  1  0  0
0  1  1  1  0  1  1  0  0  0  0  0  1
0  1  1  1  0  1  1  0  1  0  0  1  0
0  1  1  1  0  1  1  1  0  0  1  0  0
0  1  1  1  0  1  1  1  1  0  1  0  0
0  1  1  1  0  1  0  0  0  0  1  0  0
0  1  1  1  0  1  0  0  1  0  1  0  0
0  1  1  1  0  1  0  1  0  0  1  0  0
0  1  1  1  0  1  0  1  1  0  1  0  0
0  1  1  1  1  0  1  0  0  0  0  0  1
0  1  1  1  1  0  1  0  1  0  0  0  1
0  1  1  1  1  0  1  1  0  0  0  1  0
0  1  1  1  1  0  1  1  1  0  1  0  0
0  1  1  1  1  0  0  0  0  0  1  0  0
0  1  1  1  1  0  0  0  1  0  1  0  0
0  1  1  1  1  0  0  1  0  0  1  0  0
0  1  1  1  1  0  0  1  1  0  1  0  0
0  1  1  1  1  1  1  0  0  0  0  0  1
0  1  1  1  1  1  1  0  1  0  0  0  1
0  1  1  1  1  1  1  1  0  0  0  0  1
0  1  1  1  1  1  1  1  1  0  0  1  0
0  1  1  1  1  1  0  0  0  0  1  0  0
0  1  1  1  1  1  0  0  1  0  1  0  0
0  1  1  1  1  1  0  1  0  0  1  0  0
0  1  1  1  1  1  0  1  1  0  1  0  0
0  1  1  0  0  0  1  0  0  0  0  0  1
0  1  1  0  0  0  1  0  1  0  0  0  1
0  1  1  0  0  0  1  1  0  0  0  0  1
0  1  1  0  0  0  1  1  1  0  0  0  1
0  1  1  0  0  0  0  0  0  0  0  1  0
0  1  1  0  0  0  0  0  1  0  1  0  0
0  1  1  0  0  0  0  1  0  0  1  0  0
0  1  1  0  0  0  0  1  1  0  1  0  0
0  1  1  0  0  1  1  0  0  0  0  0  1
0  1  1  0  0  1  1  0  1  0  0  0  1
0  1  1  0  0  1  1  1  0  0  0  0  1
0  1  1  0  0  1  1  1  1  0  0  0  1
0  1  1  0  0  1  0  0  0  0  0  0  1
0  1  1  0  0  1  0  0  1  0  0  1  0
0  1  1  0  0  1  0  1  0  0  1  0  0
0  1  1  0  0  1  0  1  1  0  1  0  0
0  1  1  0  1  0  1  0  0  0  0  0  1
0  1  1  0  1  0  1  0  1  0  0  0  1
0  1  1  0  1  0  1  1  0  0  0  0  1
0  1  1  0  1  0  1  1  1  0  0  0  1
0  1  1  0  1  0  0  0  0  0  0  0  1
0  1  1  0  1  0  0  0  1  0  0  0  1
0  1  1  0  1  0  0  1  0  0  0  1  0
0  1  1  0  1  0  0  1  1  0  1  0  0
0  1  1  0  1  1  1  0  0  0  0  0  1
0  1  1  0  1  1  1  0  1  0  0  0  1
0  1  1  0  1  1  1  1  0  0  0  0  1
0  1  1  0  1  1  1  1  1  0  0  0  1
0  1  1  0  1  1  0  0  0  0  0  0  1
0  1  1  0  1  1  0  0  1  0  0  0  1
0  1  1  0  1  1  0  1  0  0  0  0  1
0  1  1  0  1  1  0  1  1  0  0  1  0
*/

/* Test case Numeros Primos:
C2 C1 C0 A2 A1 A0 B2 B1 B0 E R2 R1 R0
1  0  1  0  0  0  X  X  X  0  0  0  0
1  0  1  0  0  1  X  X  X  0  0  0  0
1  0  1  0  1  0  X  X  X  0  1  1  1
1  0  1  0  1  1  X  X  X  0  1  1  1
1  0  1  1  0  0  X  X  X  0  0  0  0
1  0  1  1  0  1  X  X  X  0  1  1  1
1  0  1  1  1  0  X  X  X  0  0  0  0
1  0  1  1  1  1  X  X  X  0  1  1  1
*/
